// Logisim project sandbox.circ as structural Verilog: 1 circuit, main circuit main
module main (
);

  wire Tick;
  wire [5:0] Control_p2;
  wire [31:0] adder_1_p3, PC_q;

  Clock clock_1 (.out(Tick));
  Register #(.width(32)) PC (.D(adder_1_p3), .Q(PC_q), .clk(Tick));  // open: en, clr
  Register #(.width(6)) OpCode (.D(Control_p2), .clk(Tick));  // open: en, Q, clr
  // PLA Control: pin names not known; wires that end beside it: PC_q, Control_p2
  // Adder adder_1: pin names not known; wires that end beside it: PC_q, 32'h4, adder_1_p3
  // MIPSProgramROM mipsprogramrom_1: pin names not known
endmodule
